// Logisim project logism_design.circ as structural Verilog: 25 circuits, main circuit processor
module processor (
  input  in_1,
  output [3:0] REG_OUT,
  output [3:0] REG1,
  output [3:0] REG0,
  output [3:0] OPCODE,
  output [5:0] IMM,
  output [9:0] ADRESS,
  output [8:0] COUNTER
);

  wire button_1_out, button_2_out, CPU_CLOCK;
  wire [2:0] ALUCONTROL;
  wire [17:0] ALU_OUT, Data0, Data1;

  Clock clock_1 (.out(CPU_CLOCK));
  ALU alu_1 (.OP(ALUCONTROL), .REGINPUT1(Data0), .REGINPUT2(Data1), .IMM(ADRESS[5:0]), .out_5(ALU_OUT));
  Button button_1 (.out(button_1_out));
  _9_bit_counter u_9_bit_counter_1 (.Jump({10{1'b0}}), .out_3(COUNTER), .Clock(CPU_CLOCK));
  ROM #(.addrWidth(9), .dataWidth(18)) rom_1 (.addr(COUNTER), .data({OPCODE, REG0, ADRESS}), .sel(1'b1));
  Button button_2 (.out(button_2_out));
  register_file register_file_1 (
    .READ_DATA_1(Data0), .READ_REG_1(REG0), .READ_DATA_2(Data1), .READ_REG_2(ADRESS[9:6]),
    .WRITE_REG(ADRESS[5:2]), .WRITE_DATA(ALU_OUT), .REG_WRITE_ENABLE(1'b1), .Clock(CPU_CLOCK),
    .Clear(button_2_out));
  control_unit control_unit_1 ();  // open: INPUT

  assign IMM = ADRESS[5:0];
  assign REG1 = ADRESS[9:6];
  assign REG_OUT = ADRESS[5:2];

  // Other names for the same wires on the sheet: ADDRESS[9:0] = ADRESS

  // Notes on the sheet:
  //   0000 0100 0010 110100
  //   contents of rom_1 (hex, n*v repeats v):
  //   10b4 577f 577f 1d400 21400 25740 28090 2fff0 33ff0 37ff0 3bff0
endmodule

module half_adder (
  input  A,
  input  B,
  output out_3,
  output out_4
);

  xor xor_1 (out_3, A, B);
  and and_1 (out_4, A, B);
endmodule

module full_adder (
  input  in_1,
  input  in_2,
  input  in_3,
  output out_4,
  output out_5
);

  wire and_1_out, and_2_out, xor_1_out;

  xor xor_1 (xor_1_out, in_1, in_2);
  xor xor_2 (out_4, xor_1_out, in_3);
  and and_1 (and_1_out, xor_1_out, in_3);
  and and_2 (and_2_out, in_2, in_1);
  or or_1 (out_5, and_1_out, and_2_out);
endmodule

module ALU (
  input  [17:0] REGINPUT1,
  input  [17:0] REGINPUT2,
  input  [5:0] IMM,
  input  [2:0] OP,
  output [17:0] out_5
);

  wire [17:0] ADD18_a_2, ADDIMM_a_2, AND18_a_2, ANDIMM_a_2, NAND18_a_2, NOR18_a_2, undriven;

  _18_bit_and AND18 (.A(REGINPUT2), .B(REGINPUT1), .A_2(AND18_a_2));
  _18_bit_adder ADD18 (.A(REGINPUT2), .B(REGINPUT1), .A_2(ADD18_a_2));
  Multiplexer #(.select(3), .width(18), .enable("false")) multiplexer_1 (
    .in0(ADD18_a_2), .in1(ADDIMM_a_2), .in2(AND18_a_2), .in3(ANDIMM_a_2), .in4(NOR18_a_2), .in5(NAND18_a_2),
    .out(out_5), .sel(OP));  // open: in6, in7
  _18_bit_nand NAND18 (.A(REGINPUT2), .B(REGINPUT1), .A_2(NAND18_a_2));
  _18_bit_nor NOR18 (.A(REGINPUT2), .B(REGINPUT1), .A_2(NOR18_a_2));
  _18_bit_adder ADDIMM (.A(undriven), .B(REGINPUT1), .A_2(ADDIMM_a_2));
  _18_bit_and ANDIMM (.A(undriven), .B(REGINPUT1), .A_2(ANDIMM_a_2));
endmodule

module _18_bit_adder (
  input  [17:0] A,
  input  [17:0] B,
  output [17:0] A_2
);

  wire full_adder_1_out_5, full_adder_2_out_5, full_adder_3_out_5, full_adder_4_out_5, full_adder_5_out_5,
       full_adder_6_out_5, full_adder_7_out_5, full_adder_8_out_5, full_adder_9_out_5, full_adder_10_out_5,
       full_adder_11_out_5, full_adder_12_out_5, full_adder_13_out_5, full_adder_14_out_5,
       full_adder_15_out_5, full_adder_16_out_5, full_adder_17_out_5;

  full_adder full_adder_1 (.in_1(1'b0), .in_2(B[0]), .in_3(A[0]), .out_4(A_2[0]), .out_5(full_adder_1_out_5));
  full_adder full_adder_2 (
    .in_1(full_adder_1_out_5), .in_2(B[1]), .in_3(A[1]), .out_4(A_2[1]), .out_5(full_adder_2_out_5));
  full_adder full_adder_3 (
    .in_1(full_adder_2_out_5), .in_2(B[2]), .in_3(A[2]), .out_4(A_2[2]), .out_5(full_adder_3_out_5));
  full_adder full_adder_4 (
    .in_1(full_adder_3_out_5), .in_2(B[3]), .in_3(A[3]), .out_4(A_2[3]), .out_5(full_adder_4_out_5));
  full_adder full_adder_5 (
    .in_1(full_adder_4_out_5), .in_2(B[4]), .in_3(A[4]), .out_4(A_2[4]), .out_5(full_adder_5_out_5));
  full_adder full_adder_6 (
    .in_1(full_adder_5_out_5), .in_2(B[5]), .in_3(A[5]), .out_4(A_2[5]), .out_5(full_adder_6_out_5));
  full_adder full_adder_7 (
    .in_1(full_adder_6_out_5), .in_2(B[6]), .in_3(A[6]), .out_4(A_2[6]), .out_5(full_adder_7_out_5));
  full_adder full_adder_8 (
    .in_1(full_adder_7_out_5), .in_2(B[7]), .in_3(A[7]), .out_4(A_2[7]), .out_5(full_adder_8_out_5));
  full_adder full_adder_9 (
    .in_1(full_adder_8_out_5), .in_2(B[8]), .in_3(A[8]), .out_4(A_2[8]), .out_5(full_adder_9_out_5));
  full_adder full_adder_10 (
    .in_1(full_adder_9_out_5), .in_2(B[9]), .in_3(A[9]), .out_4(A_2[9]), .out_5(full_adder_10_out_5));
  full_adder full_adder_11 (
    .in_1(full_adder_10_out_5), .in_2(B[10]), .in_3(A[10]), .out_4(A_2[10]), .out_5(full_adder_11_out_5));
  full_adder full_adder_12 (
    .in_1(full_adder_11_out_5), .in_2(A[11]), .in_3(B[11]), .out_4(A_2[11]), .out_5(full_adder_12_out_5));
  full_adder full_adder_13 (
    .in_1(full_adder_12_out_5), .in_2(A[12]), .in_3(B[12]), .out_4(A_2[12]), .out_5(full_adder_13_out_5));
  full_adder full_adder_14 (
    .in_1(full_adder_13_out_5), .in_2(A[13]), .in_3(B[13]), .out_4(A_2[13]), .out_5(full_adder_14_out_5));
  full_adder full_adder_15 (
    .in_1(full_adder_14_out_5), .in_2(A[14]), .in_3(B[14]), .out_4(A_2[14]), .out_5(full_adder_15_out_5));
  full_adder full_adder_16 (
    .in_1(full_adder_15_out_5), .in_2(B[15]), .in_3(A[15]), .out_4(A_2[15]), .out_5(full_adder_16_out_5));
  full_adder full_adder_17 (
    .in_1(full_adder_16_out_5), .in_2(B[16]), .in_3(A[16]), .out_4(A_2[16]), .out_5(full_adder_17_out_5));
  full_adder full_adder_18 (.in_1(full_adder_17_out_5), .in_2(A[17]), .in_3(B[17]), .out_4(A_2[17]));  // open: out_5
endmodule

module _18_bit_and (
  input  [17:0] A,
  input  [17:0] B,
  output [17:0] A_2
);

  and and_1 (A_2[0], A[0], B[0]);
  and and_2 (A_2[1], A[1], B[1]);
  and and_3 (A_2[2], A[2], B[2]);
  and and_4 (A_2[3], A[3], B[3]);
  and and_5 (A_2[4], A[4], B[4]);
  and and_6 (A_2[5], A[5], B[5]);
  and and_7 (A_2[6], A[6], B[6]);
  and and_8 (A_2[7], A[7], B[7]);
  and and_9 (A_2[8], A[8], B[8]);
  and and_10 (A_2[9], A[9], B[9]);
  and and_11 (A_2[10], A[10], B[10]);
  and and_12 (A_2[11], A[11], B[11]);
  and and_13 (A_2[12], A[12], B[12]);
  and and_14 (A_2[13], A[13], B[13]);
  and and_15 (A_2[14], A[14], B[14]);
  and and_16 (A_2[15], A[15], B[15]);
  and and_17 (A_2[16], A[16], B[16]);
  and and_18 (A_2[17], A[17], B[17]);
endmodule

module _18_bit_nand (
  input  [17:0] A,
  input  [17:0] B,
  output [17:0] A_2
);

  nand nand_1 (A_2[0], A[0], B[0]);
  nand nand_2 (A_2[1], A[1], B[1]);
  nand nand_3 (A_2[2], A[2], B[2]);
  nand nand_4 (A_2[3], A[3], B[3]);
  nand nand_5 (A_2[4], A[4], B[4]);
  nand nand_6 (A_2[5], A[5], B[5]);
  nand nand_7 (A_2[6], A[6], B[6]);
  nand nand_8 (A_2[7], A[7], B[7]);
  nand nand_9 (A_2[8], A[8], B[8]);
  nand nand_10 (A_2[9], A[9], B[9]);
  nand nand_11 (A_2[10], A[10], B[10]);
  nand nand_12 (A_2[11], A[11], B[11]);
  nand nand_13 (A_2[12], A[12], B[12]);
  nand nand_14 (A_2[13], A[13], B[13]);
  nand nand_15 (A_2[14], A[14], B[14]);
  nand nand_16 (A_2[15], A[15], B[15]);
  nand nand_17 (A_2[16], A[16], B[16]);
  nand nand_18 (A_2[17], A[17], B[17]);
endmodule

module _18_bit_nor (
  input  [17:0] A,
  input  [17:0] B,
  output [17:0] A_2
);

  nor nor_1 (A_2[0], A[0], B[0]);
  nor nor_2 (A_2[1], A[1], B[1]);
  nor nor_3 (A_2[2], A[2], B[2]);
  nor nor_4 (A_2[3], A[3], B[3]);
  nor nor_5 (A_2[4], A[4], B[4]);
  nor nor_6 (A_2[5], A[5], B[5]);
  nor nor_7 (A_2[6], A[6], B[6]);
  nor nor_8 (A_2[7], A[7], B[7]);
  nor nor_9 (A_2[8], A[8], B[8]);
  nor nor_10 (A_2[9], A[9], B[9]);
  nor nor_11 (A_2[10], A[10], B[10]);
  nor nor_12 (A_2[11], A[11], B[11]);
  nor nor_13 (A_2[12], A[12], B[12]);
  nor nor_14 (A_2[13], A[13], B[13]);
  nor nor_15 (A_2[14], A[14], B[14]);
  nor nor_16 (A_2[15], A[15], B[15]);
  nor nor_17 (A_2[16], A[16], B[16]);
  nor nor_18 (A_2[17], A[17], B[17]);
endmodule

module d_latch (
  input  D,
  input  Clock,
  output Q
);

  wire and_1_out, and_2_out, nor_1_out, not_1_out;

  not not_1 (not_1_out, D);
  and and_1 (and_1_out, D, Clock);
  and and_2 (and_2_out, not_1_out, Clock);
  nor nor_1 (nor_1_out, and_1_out, Q);
  nor nor_2 (Q, nor_1_out, and_2_out);
endmodule

module d_flip_flop (
  input  D,
  input  Clock,
  output out_3
);

  wire d_latch_1_q, not_1_out;

  d_latch d_latch_1 (.D(D), .Clock(Clock), .Q(d_latch_1_q));
  not not_1 (not_1_out, Clock);
  d_latch d_latch_2 (.D(d_latch_1_q), .Clock(not_1_out), .Q(out_3));
endmodule

module _18_bit_register (
  input  [17:0] Input,
  input  Enable,
  input  Clock,
  input  Clear,
  output [17:0] Output
);

  wire and_1_out, not_1_out;
  wire [17:0] d_flip_flop_1_out_3, multiplexer_1_out, not_2_out;

  and and_1 (and_1_out, Enable, Clock);
  not not_1 (not_1_out, and_1_out);
  d_flip_flop d_flip_flop_1 (.D(Input[0]), .Clock(not_1_out), .out_3(d_flip_flop_1_out_3[0]));
  d_flip_flop d_flip_flop_2 (.D(Input[1]), .Clock(not_1_out), .out_3(d_flip_flop_1_out_3[1]));
  d_flip_flop d_flip_flop_3 (.D(Input[2]), .Clock(not_1_out), .out_3(d_flip_flop_1_out_3[2]));
  d_flip_flop d_flip_flop_4 (.D(Input[3]), .Clock(not_1_out), .out_3(d_flip_flop_1_out_3[3]));
  d_flip_flop d_flip_flop_5 (.D(Input[4]), .Clock(not_1_out), .out_3(d_flip_flop_1_out_3[4]));
  d_flip_flop d_flip_flop_6 (.D(Input[5]), .Clock(not_1_out), .out_3(d_flip_flop_1_out_3[5]));
  d_flip_flop d_flip_flop_7 (.D(Input[6]), .Clock(not_1_out), .out_3(d_flip_flop_1_out_3[6]));
  d_flip_flop d_flip_flop_8 (.D(Input[7]), .Clock(not_1_out), .out_3(d_flip_flop_1_out_3[7]));
  d_flip_flop d_flip_flop_9 (.D(Input[8]), .Clock(not_1_out), .out_3(d_flip_flop_1_out_3[8]));
  d_flip_flop d_flip_flop_10 (.D(Input[9]), .Clock(not_1_out), .out_3(d_flip_flop_1_out_3[9]));
  d_flip_flop d_flip_flop_11 (.D(Input[10]), .Clock(not_1_out), .out_3(d_flip_flop_1_out_3[10]));
  d_flip_flop d_flip_flop_12 (.D(Input[11]), .Clock(not_1_out), .out_3(d_flip_flop_1_out_3[11]));
  d_flip_flop d_flip_flop_13 (.D(Input[12]), .Clock(not_1_out), .out_3(d_flip_flop_1_out_3[12]));
  d_flip_flop d_flip_flop_14 (.D(Input[13]), .Clock(not_1_out), .out_3(d_flip_flop_1_out_3[13]));
  d_flip_flop d_flip_flop_15 (.D(Input[14]), .Clock(not_1_out), .out_3(d_flip_flop_1_out_3[14]));
  d_flip_flop d_flip_flop_16 (.D(Input[15]), .Clock(not_1_out), .out_3(d_flip_flop_1_out_3[15]));
  d_flip_flop d_flip_flop_17 (.D(Input[16]), .Clock(not_1_out), .out_3(d_flip_flop_1_out_3[16]));
  d_flip_flop d_flip_flop_18 (.D(Input[17]), .Clock(not_1_out), .out_3(d_flip_flop_1_out_3[17]));
  assign not_2_out = ~{18{1'b0}};  // NOT_Gate not_2, 18 bits wide
  Multiplexer #(.width(18)) multiplexer_1 (
    .in0(not_2_out), .in1({18{1'b0}}), .out(multiplexer_1_out), .sel(Clear));  // open: en
  assign Output = multiplexer_1_out & d_flip_flop_1_out_3;  // AND_Gate and_2, 18 bits wide
endmodule

module half_comparator (
  input  A,
  input  B,
  output GREATERTHAN,
  output LESSTHAN,
  output EQUAL
);

  wire and_3_out, and_4_out, not_1_out, not_2_out;

  not not_1 (not_1_out, A);
  not not_2 (not_2_out, B);
  and and_1 (GREATERTHAN, A, not_2_out);
  and and_2 (LESSTHAN, not_1_out, B);
  and and_3 (and_3_out, A, B);
  and and_4 (and_4_out, not_1_out, not_2_out);
  or or_1 (EQUAL, and_3_out, and_4_out);
endmodule

module full_comparator (
  input  A,
  input  B,
  input  GTB,
  input  LSTB,
  input  EQB,
  output GREATERTHAN,
  output LESSTHAN,
  output EQUAL
);

  wire and_1_out, and_2_out, and_3_out, and_4_out, and_5_out, and_6_out, not_1_out, not_2_out, not_3_out,
       not_4_out, or_1_out;

  not not_1 (not_1_out, B);
  not not_2 (not_2_out, A);
  not not_3 (not_3_out, A);
  not not_4 (not_4_out, B);
  and and_1 (and_1_out, A, not_1_out);
  and and_2 (and_2_out, not_2_out, B);
  and and_3 (and_3_out, A, B);
  or or_1 (or_1_out, and_3_out, and_4_out);
  and and_4 (and_4_out, not_3_out, not_4_out);
  and and_5 (and_5_out, and_1_out, EQB);
  and and_6 (and_6_out, EQB, and_2_out);
  and and_7 (EQUAL, EQB, or_1_out);
  or or_2 (GREATERTHAN, and_5_out, GTB);
  or or_3 (LESSTHAN, and_6_out, LSTB);
endmodule

module _18_bit_comparator (
  input  [17:0] A,
  input  [17:0] B,
  output GREATERTHAN,
  output LESSTHAN,
  output EQUAL
);

  wire full_comparator_1_equal, full_comparator_1_greaterthan, full_comparator_1_lessthan,
       full_comparator_2_equal, full_comparator_2_greaterthan, full_comparator_2_lessthan,
       full_comparator_3_equal, full_comparator_3_greaterthan, full_comparator_3_lessthan,
       full_comparator_4_equal, full_comparator_4_greaterthan, full_comparator_4_lessthan,
       full_comparator_5_equal, full_comparator_5_greaterthan, full_comparator_5_lessthan,
       full_comparator_6_equal, full_comparator_6_greaterthan, full_comparator_6_lessthan,
       full_comparator_7_equal, full_comparator_7_greaterthan, full_comparator_7_lessthan,
       full_comparator_8_equal, full_comparator_8_greaterthan, full_comparator_8_lessthan,
       full_comparator_9_equal, full_comparator_9_greaterthan, full_comparator_9_lessthan,
       full_comparator_10_equal, full_comparator_10_greaterthan, full_comparator_10_lessthan,
       full_comparator_11_equal, full_comparator_11_greaterthan, full_comparator_11_lessthan,
       full_comparator_12_equal, full_comparator_12_greaterthan, full_comparator_12_lessthan,
       full_comparator_13_equal, full_comparator_13_greaterthan, full_comparator_13_lessthan,
       full_comparator_14_equal, full_comparator_14_greaterthan, full_comparator_14_lessthan,
       full_comparator_15_equal, full_comparator_15_greaterthan, full_comparator_15_lessthan,
       full_comparator_16_equal, full_comparator_16_greaterthan, full_comparator_16_lessthan,
       half_comparator_1_equal, half_comparator_1_greaterthan, half_comparator_1_lessthan;

  half_comparator half_comparator_1 (
    .A(A[17]), .B(B[17]), .GREATERTHAN(half_comparator_1_greaterthan), .LESSTHAN(half_comparator_1_lessthan),
    .EQUAL(half_comparator_1_equal));
  full_comparator full_comparator_1 (
    .A(A[16]), .B(B[16]), .GTB(half_comparator_1_greaterthan), .LSTB(half_comparator_1_lessthan),
    .EQB(half_comparator_1_equal), .GREATERTHAN(full_comparator_1_greaterthan),
    .LESSTHAN(full_comparator_1_lessthan), .EQUAL(full_comparator_1_equal));
  full_comparator full_comparator_2 (
    .A(A[15]), .B(B[15]), .GTB(full_comparator_1_greaterthan), .LSTB(full_comparator_1_lessthan),
    .EQB(full_comparator_1_equal), .GREATERTHAN(full_comparator_2_greaterthan),
    .LESSTHAN(full_comparator_2_lessthan), .EQUAL(full_comparator_2_equal));
  full_comparator full_comparator_3 (
    .A(A[14]), .B(B[14]), .GTB(full_comparator_2_greaterthan), .LSTB(full_comparator_2_lessthan),
    .EQB(full_comparator_2_equal), .GREATERTHAN(full_comparator_3_greaterthan),
    .LESSTHAN(full_comparator_3_lessthan), .EQUAL(full_comparator_3_equal));
  full_comparator full_comparator_4 (
    .A(B[12]), .B(A[12]), .GTB(full_comparator_5_greaterthan), .LSTB(full_comparator_5_lessthan),
    .EQB(full_comparator_5_equal), .GREATERTHAN(full_comparator_4_greaterthan),
    .LESSTHAN(full_comparator_4_lessthan), .EQUAL(full_comparator_4_equal));
  full_comparator full_comparator_5 (
    .A(A[13]), .B(B[13]), .GTB(full_comparator_3_greaterthan), .LSTB(full_comparator_3_lessthan),
    .EQB(full_comparator_3_equal), .GREATERTHAN(full_comparator_5_greaterthan),
    .LESSTHAN(full_comparator_5_lessthan), .EQUAL(full_comparator_5_equal));
  full_comparator full_comparator_6 (
    .A(A[11]), .B(B[11]), .GTB(full_comparator_4_greaterthan), .LSTB(full_comparator_4_lessthan),
    .EQB(full_comparator_4_equal), .GREATERTHAN(full_comparator_6_greaterthan),
    .LESSTHAN(full_comparator_6_lessthan), .EQUAL(full_comparator_6_equal));
  full_comparator full_comparator_7 (
    .A(A[10]), .B(B[10]), .GTB(full_comparator_6_greaterthan), .LSTB(full_comparator_6_lessthan),
    .EQB(full_comparator_6_equal), .GREATERTHAN(full_comparator_7_greaterthan),
    .LESSTHAN(full_comparator_7_lessthan), .EQUAL(full_comparator_7_equal));
  full_comparator full_comparator_8 (
    .A(A[9]), .B(B[9]), .GTB(full_comparator_7_greaterthan), .LSTB(full_comparator_7_lessthan),
    .EQB(full_comparator_7_equal), .GREATERTHAN(full_comparator_8_greaterthan),
    .LESSTHAN(full_comparator_8_lessthan), .EQUAL(full_comparator_8_equal));
  full_comparator full_comparator_9 (
    .A(A[8]), .B(B[8]), .GTB(full_comparator_8_greaterthan), .LSTB(full_comparator_8_lessthan),
    .EQB(full_comparator_8_equal), .GREATERTHAN(full_comparator_9_greaterthan),
    .LESSTHAN(full_comparator_9_lessthan), .EQUAL(full_comparator_9_equal));
  full_comparator full_comparator_10 (
    .A(B[7]), .B(A[7]), .GTB(full_comparator_9_greaterthan), .LSTB(full_comparator_9_lessthan),
    .EQB(full_comparator_9_equal), .GREATERTHAN(full_comparator_10_greaterthan),
    .LESSTHAN(full_comparator_10_lessthan), .EQUAL(full_comparator_10_equal));
  full_comparator full_comparator_11 (
    .A(B[6]), .B(A[6]), .GTB(full_comparator_10_greaterthan), .LSTB(full_comparator_10_lessthan),
    .EQB(full_comparator_10_equal), .GREATERTHAN(full_comparator_11_greaterthan),
    .LESSTHAN(full_comparator_11_lessthan), .EQUAL(full_comparator_11_equal));
  full_comparator full_comparator_12 (
    .A(A[5]), .B(B[5]), .GTB(full_comparator_11_greaterthan), .LSTB(full_comparator_11_lessthan),
    .EQB(full_comparator_11_equal), .GREATERTHAN(full_comparator_12_greaterthan),
    .LESSTHAN(full_comparator_12_lessthan), .EQUAL(full_comparator_12_equal));
  full_comparator full_comparator_13 (
    .A(A[4]), .B(B[4]), .GTB(full_comparator_12_greaterthan), .LSTB(full_comparator_12_lessthan),
    .EQB(full_comparator_12_equal), .GREATERTHAN(full_comparator_13_greaterthan),
    .LESSTHAN(full_comparator_13_lessthan), .EQUAL(full_comparator_13_equal));
  full_comparator full_comparator_14 (
    .A(A[3]), .B(B[3]), .GTB(full_comparator_13_greaterthan), .LSTB(full_comparator_13_lessthan),
    .EQB(full_comparator_13_equal), .GREATERTHAN(full_comparator_14_greaterthan),
    .LESSTHAN(full_comparator_14_lessthan), .EQUAL(full_comparator_14_equal));
  full_comparator full_comparator_15 (
    .A(A[2]), .B(B[2]), .GTB(full_comparator_14_greaterthan), .LSTB(full_comparator_14_lessthan),
    .EQB(full_comparator_14_equal), .GREATERTHAN(full_comparator_15_greaterthan),
    .LESSTHAN(full_comparator_15_lessthan), .EQUAL(full_comparator_15_equal));
  full_comparator full_comparator_16 (
    .A(A[1]), .B(B[1]), .GTB(full_comparator_15_greaterthan), .LSTB(full_comparator_15_lessthan),
    .EQB(full_comparator_15_equal), .GREATERTHAN(full_comparator_16_greaterthan),
    .LESSTHAN(full_comparator_16_lessthan), .EQUAL(full_comparator_16_equal));
  full_comparator full_comparator_17 (
    .A(A[0]), .B(B[0]), .GTB(full_comparator_16_greaterthan), .LSTB(full_comparator_16_lessthan),
    .EQB(full_comparator_16_equal), .GREATERTHAN(GREATERTHAN), .LESSTHAN(LESSTHAN), .EQUAL(EQUAL));
endmodule

module half_subtractor (
  input  A,
  input  B,
  output DIFFERENCE,
  output BORROW
);

  wire not_1_out, not_2_out;

  not not_1 (not_1_out, A);
  not not_2 (not_2_out, B);
  xor xor_1 (DIFFERENCE, A, B);
  and and_1 (BORROW, not_1_out, B);
endmodule

module full_subtractor (
  input  BFNS,
  input  A,
  input  B,
  output DIFFERENCE,
  output BORROW
);

  wire and_1_out, and_2_out, and_3_out, not_1_out, not_2_out, not_3_out;

  not not_1 (not_1_out, A);
  not not_2 (not_2_out, B);
  not not_3 (not_3_out, BFNS);
  and and_1 (and_1_out, B, BFNS);
  and and_2 (and_2_out, not_1_out, BFNS);
  and and_3 (and_3_out, not_1_out, B);
  ExactlyOne xor_1 (.out(DIFFERENCE), .in0(A), .in1(B), .in2(BFNS));
  or or_1 (BORROW, and_1_out, and_2_out, and_3_out);
endmodule

module _18_bit_subtractor (
  input  [17:0] A,
  input  [17:0] B,
  output [17:0] A_2
);

  wire full_subtractor_1_borrow, full_subtractor_2_borrow, full_subtractor_3_borrow,
       full_subtractor_4_borrow, full_subtractor_5_borrow, full_subtractor_6_borrow,
       full_subtractor_7_borrow, full_subtractor_8_borrow, full_subtractor_9_borrow,
       full_subtractor_10_borrow, full_subtractor_11_borrow, full_subtractor_12_borrow,
       full_subtractor_13_borrow, full_subtractor_14_borrow, full_subtractor_15_borrow,
       full_subtractor_16_borrow, full_subtractor_17_borrow, full_subtractor_18_borrow;

  full_subtractor full_subtractor_1 (
    .BFNS(1'b0), .A(A[0]), .B(B[0]), .DIFFERENCE(A_2[0]), .BORROW(full_subtractor_1_borrow));
  full_subtractor full_subtractor_2 (
    .BFNS(full_subtractor_1_borrow), .A(A[1]), .B(B[1]), .DIFFERENCE(A_2[1]),
    .BORROW(full_subtractor_2_borrow));
  full_subtractor full_subtractor_3 (
    .BFNS(full_subtractor_2_borrow), .A(A[2]), .B(B[2]), .DIFFERENCE(A_2[2]),
    .BORROW(full_subtractor_3_borrow));
  full_subtractor full_subtractor_4 (
    .BFNS(full_subtractor_3_borrow), .A(A[3]), .B(B[3]), .DIFFERENCE(A_2[3]),
    .BORROW(full_subtractor_4_borrow));
  full_subtractor full_subtractor_5 (
    .BFNS(full_subtractor_4_borrow), .A(A[4]), .B(B[4]), .DIFFERENCE(A_2[4]),
    .BORROW(full_subtractor_5_borrow));
  full_subtractor full_subtractor_6 (
    .BFNS(full_subtractor_5_borrow), .A(A[5]), .B(B[5]), .DIFFERENCE(A_2[5]),
    .BORROW(full_subtractor_6_borrow));
  full_subtractor full_subtractor_7 (
    .BFNS(full_subtractor_6_borrow), .A(A[6]), .B(B[6]), .DIFFERENCE(A_2[6]),
    .BORROW(full_subtractor_7_borrow));
  full_subtractor full_subtractor_8 (
    .BFNS(full_subtractor_7_borrow), .A(A[7]), .B(B[7]), .DIFFERENCE(A_2[7]),
    .BORROW(full_subtractor_8_borrow));
  full_subtractor full_subtractor_9 (
    .BFNS(full_subtractor_8_borrow), .A(A[8]), .B(B[8]), .DIFFERENCE(A_2[8]),
    .BORROW(full_subtractor_9_borrow));
  full_subtractor full_subtractor_10 (
    .BFNS(full_subtractor_9_borrow), .A(A[9]), .B(B[9]), .DIFFERENCE(A_2[9]),
    .BORROW(full_subtractor_10_borrow));
  full_subtractor full_subtractor_11 (
    .BFNS(full_subtractor_10_borrow), .A(A[10]), .B(B[10]), .DIFFERENCE(A_2[10]),
    .BORROW(full_subtractor_11_borrow));
  full_subtractor full_subtractor_12 (
    .BFNS(full_subtractor_11_borrow), .A(A[11]), .B(B[11]), .DIFFERENCE(A_2[11]),
    .BORROW(full_subtractor_12_borrow));
  full_subtractor full_subtractor_13 (
    .BFNS(full_subtractor_12_borrow), .A(A[12]), .B(B[12]), .DIFFERENCE(A_2[12]),
    .BORROW(full_subtractor_13_borrow));
  full_subtractor full_subtractor_14 (
    .BFNS(full_subtractor_13_borrow), .A(A[13]), .B(B[13]), .DIFFERENCE(A_2[13]),
    .BORROW(full_subtractor_14_borrow));
  full_subtractor full_subtractor_15 (
    .BFNS(full_subtractor_14_borrow), .A(A[14]), .B(B[14]), .DIFFERENCE(A_2[14]),
    .BORROW(full_subtractor_15_borrow));
  full_subtractor full_subtractor_16 (
    .BFNS(full_subtractor_15_borrow), .A(A[15]), .B(B[15]), .DIFFERENCE(A_2[15]),
    .BORROW(full_subtractor_16_borrow));
  full_subtractor full_subtractor_17 (
    .BFNS(full_subtractor_16_borrow), .A(A[16]), .B(B[16]), .DIFFERENCE(A_2[16]),
    .BORROW(full_subtractor_17_borrow));
  full_subtractor full_subtractor_18 (
    .BFNS(full_subtractor_17_borrow), .A(A[17]), .B(B[17]), .DIFFERENCE(A_2[17]),
    .BORROW(full_subtractor_18_borrow));
endmodule

module _10_18_bit_extender (
  input  [9:0] in_1,
  output [17:0] out_2
);

  Multiplexer #(.width(8), .enable("false")) multiplexer_1 (
    .in0({8{1'b0}}), .in1({8{1'b1}}), .out(out_2[17:10]), .sel(in_1[9]));

  assign out_2[9:0] = in_1;
endmodule

module _9_bit_register (
  input  [8:0] in_1,
  input  Reset,
  input  Clock,
  output [8:0] Output
);

  wire or_1_out;
  wire [8:0] multiplexer_1_out;

  Multiplexer #(.width(9), .enable("false")) multiplexer_1 (
    .in0(in_1), .in1({9{1'b0}}), .out(multiplexer_1_out), .sel(Reset));
  d_flip_flop d_flip_flop_1 (.D(multiplexer_1_out[0]), .Clock(or_1_out), .out_3(Output[0]));
  d_flip_flop d_flip_flop_2 (.D(multiplexer_1_out[1]), .Clock(or_1_out), .out_3(Output[1]));
  d_flip_flop d_flip_flop_3 (.D(multiplexer_1_out[2]), .Clock(or_1_out), .out_3(Output[2]));
  d_flip_flop d_flip_flop_4 (.D(multiplexer_1_out[3]), .Clock(or_1_out), .out_3(Output[3]));
  d_flip_flop d_flip_flop_5 (.D(multiplexer_1_out[4]), .Clock(or_1_out), .out_3(Output[4]));
  d_flip_flop d_flip_flop_6 (.D(multiplexer_1_out[5]), .Clock(or_1_out), .out_3(Output[5]));
  d_flip_flop d_flip_flop_7 (.D(multiplexer_1_out[6]), .Clock(or_1_out), .out_3(Output[6]));
  d_flip_flop d_flip_flop_8 (.D(multiplexer_1_out[7]), .Clock(or_1_out), .out_3(Output[7]));
  d_flip_flop d_flip_flop_9 (.D(multiplexer_1_out[8]), .Clock(or_1_out), .out_3(Output[8]));
  or or_1 (or_1_out, Reset, Clock);
endmodule

module _9_bit_incrementer (
  input  [8:0] main,
  input  [8:0] Jump,
  output [8:0] out_3
);

  wire full_adder_1_out_5, full_adder_2_out_5, full_adder_3_out_5, full_adder_4_out_5, full_adder_5_out_5,
       full_adder_6_out_5, full_adder_7_out_5, full_adder_8_out_5, full_adder_9_out_5, nor_1_out;
  wire [8:0] multiplexer_1_out;

  nor nor_1 (nor_1_out, Jump[0], Jump[1], Jump[2], Jump[3], Jump[4], Jump[5], Jump[6], Jump[7], Jump[8]);
  Multiplexer #(.width(9), .enable("false")) multiplexer_1 (
    .in0(Jump), .in1(9'h1), .out(multiplexer_1_out), .sel(nor_1_out));
  full_adder full_adder_1 (
    .in_1(1'b0), .in_2(main[0]), .in_3(multiplexer_1_out[0]), .out_4(out_3[0]), .out_5(full_adder_1_out_5));
  full_adder full_adder_2 (
    .in_1(full_adder_1_out_5), .in_2(main[1]), .in_3(multiplexer_1_out[1]), .out_4(out_3[1]),
    .out_5(full_adder_2_out_5));
  full_adder full_adder_3 (
    .in_1(full_adder_2_out_5), .in_2(main[2]), .in_3(multiplexer_1_out[2]), .out_4(out_3[2]),
    .out_5(full_adder_3_out_5));
  full_adder full_adder_4 (
    .in_1(full_adder_3_out_5), .in_2(main[3]), .in_3(multiplexer_1_out[3]), .out_4(out_3[3]),
    .out_5(full_adder_4_out_5));
  full_adder full_adder_5 (
    .in_1(full_adder_4_out_5), .in_2(main[4]), .in_3(multiplexer_1_out[4]), .out_4(out_3[4]),
    .out_5(full_adder_5_out_5));
  full_adder full_adder_6 (
    .in_1(full_adder_5_out_5), .in_2(main[5]), .in_3(multiplexer_1_out[5]), .out_4(out_3[5]),
    .out_5(full_adder_6_out_5));
  full_adder full_adder_7 (
    .in_1(full_adder_6_out_5), .in_2(main[6]), .in_3(multiplexer_1_out[6]), .out_4(out_3[6]),
    .out_5(full_adder_7_out_5));
  full_adder full_adder_8 (
    .in_1(full_adder_7_out_5), .in_2(main[7]), .in_3(multiplexer_1_out[7]), .out_4(out_3[7]),
    .out_5(full_adder_8_out_5));
  full_adder full_adder_9 (
    .in_1(full_adder_8_out_5), .in_2(main[8]), .in_3(multiplexer_1_out[8]), .out_4(out_3[8]),
    .out_5(full_adder_9_out_5));
endmodule

module _9_bit_counter (
  input  [9:0] Jump,
  input  Clock,
  output [8:0] out_3
);

  wire button_1_out, not_1_out;
  wire [8:0] controlled_buffer_1_out, n9_bit_decrementer_1_out_3, n9_bit_incrementer_1_out_3;

  _9_bit_decrementer u_9_bit_decrementer_1 (.main(out_3), .Jump(Jump[8:0]), .out_3(n9_bit_decrementer_1_out_3));
  assign controlled_buffer_1_out = Jump[9] ? n9_bit_decrementer_1_out_3 : 9'bz;  // Controlled_Buffer controlled_buffer_1
  not not_1 (not_1_out, Jump[9]);
  assign controlled_buffer_1_out = not_1_out ? n9_bit_incrementer_1_out_3 : 9'bz;  // Controlled_Buffer controlled_buffer_2
  _9_bit_incrementer u_9_bit_incrementer_1 (.main(out_3), .Jump(Jump[8:0]), .out_3(n9_bit_incrementer_1_out_3));
  Button button_1 (.out(button_1_out));
  _9_bit_register u_9_bit_register_1 (
    .in_1(controlled_buffer_1_out), .Clock(Clock), .Output(out_3), .Reset(button_1_out));
endmodule

module _9_bit_decrementer (
  input  [8:0] main,
  input  [8:0] Jump,
  output [8:0] out_3
);

  wire full_subtractor_1_borrow, full_subtractor_2_borrow, full_subtractor_3_borrow,
       full_subtractor_4_borrow, full_subtractor_5_borrow, full_subtractor_6_borrow,
       full_subtractor_7_borrow, full_subtractor_8_borrow, full_subtractor_9_borrow, nor_1_out;
  wire [8:0] multiplexer_1_out;

  nor nor_1 (nor_1_out, Jump[0], Jump[1], Jump[2], Jump[3], Jump[4], Jump[5], Jump[6], Jump[7], Jump[8]);
  Multiplexer #(.width(9), .enable("false")) multiplexer_1 (
    .in0(Jump), .in1({9{1'b0}}), .out(multiplexer_1_out), .sel(nor_1_out));
  full_subtractor full_subtractor_1 (
    .BFNS(1'b0), .A(main[0]), .B(multiplexer_1_out[0]), .DIFFERENCE(out_3[0]),
    .BORROW(full_subtractor_1_borrow));
  full_subtractor full_subtractor_2 (
    .BFNS(full_subtractor_1_borrow), .A(main[1]), .B(multiplexer_1_out[1]), .DIFFERENCE(out_3[1]),
    .BORROW(full_subtractor_2_borrow));
  full_subtractor full_subtractor_3 (
    .BFNS(full_subtractor_2_borrow), .A(main[2]), .B(multiplexer_1_out[2]), .DIFFERENCE(out_3[2]),
    .BORROW(full_subtractor_3_borrow));
  full_subtractor full_subtractor_4 (
    .BFNS(full_subtractor_3_borrow), .A(main[3]), .B(multiplexer_1_out[3]), .DIFFERENCE(out_3[3]),
    .BORROW(full_subtractor_4_borrow));
  full_subtractor full_subtractor_5 (
    .BFNS(full_subtractor_4_borrow), .A(main[4]), .B(multiplexer_1_out[4]), .DIFFERENCE(out_3[4]),
    .BORROW(full_subtractor_5_borrow));
  full_subtractor full_subtractor_6 (
    .BFNS(full_subtractor_5_borrow), .A(main[5]), .B(multiplexer_1_out[5]), .DIFFERENCE(out_3[5]),
    .BORROW(full_subtractor_6_borrow));
  full_subtractor full_subtractor_7 (
    .BFNS(full_subtractor_6_borrow), .A(main[6]), .B(multiplexer_1_out[6]), .DIFFERENCE(out_3[6]),
    .BORROW(full_subtractor_7_borrow));
  full_subtractor full_subtractor_8 (
    .BFNS(full_subtractor_7_borrow), .A(main[7]), .B(multiplexer_1_out[7]), .DIFFERENCE(out_3[7]),
    .BORROW(full_subtractor_8_borrow));
  full_subtractor full_subtractor_9 (
    .BFNS(full_subtractor_8_borrow), .A(main[8]), .B(multiplexer_1_out[8]), .DIFFERENCE(out_3[8]),
    .BORROW(full_subtractor_9_borrow));
endmodule

module register_file (
  input  [3:0] READ_REG_1,
  input  [3:0] READ_REG_2,
  input  [3:0] WRITE_REG,
  input  [17:0] WRITE_DATA,
  input  REG_WRITE_ENABLE,
  input  Clock,
  input  Clear,
  output [17:0] READ_DATA_1,
  output [17:0] READ_DATA_2
);

  wire and_1_out, and_2_out, and_3_out, and_4_out, and_5_out, and_6_out, and_7_out, and_8_out, and_9_out,
       and_10_out, and_11_out, and_12_out, and_13_out, and_14_out, and_15_out, and_16_out, decoder_1_out0,
       decoder_1_out1, decoder_1_out2, decoder_1_out3, decoder_1_out4, decoder_1_out5, decoder_1_out6,
       decoder_1_out7, decoder_1_out8, decoder_1_out9, decoder_1_out10, decoder_1_out11, decoder_1_out12,
       decoder_1_out13, decoder_1_out14, decoder_1_out15;
  wire [17:0] REG0_output, REG1_output, REG2_output, REG3_output, REG4_output, REG5_output, REG6_output,
       REG7_output, REG8_output, REG9_output, REG10_output, REG11_output, REG12_output, REG13_output,
       REG14_output, REG15_output;

  Decoder #(.select(4), .enable("false")) decoder_1 (
    .out0(decoder_1_out0), .out1(decoder_1_out1), .out2(decoder_1_out2), .out3(decoder_1_out3),
    .out4(decoder_1_out4), .out5(decoder_1_out5), .out6(decoder_1_out6), .out7(decoder_1_out7),
    .out8(decoder_1_out8), .out9(decoder_1_out9), .out10(decoder_1_out10), .out11(decoder_1_out11),
    .out12(decoder_1_out12), .out13(decoder_1_out13), .out14(decoder_1_out14), .out15(decoder_1_out15),
    .sel(WRITE_REG));
  and and_1 (and_1_out, REG_WRITE_ENABLE, decoder_1_out0);
  and and_2 (and_2_out, REG_WRITE_ENABLE, decoder_1_out1);
  and and_3 (and_3_out, REG_WRITE_ENABLE, decoder_1_out2);
  and and_4 (and_4_out, REG_WRITE_ENABLE, decoder_1_out3);
  and and_5 (and_5_out, REG_WRITE_ENABLE, decoder_1_out4);
  and and_6 (and_6_out, REG_WRITE_ENABLE, decoder_1_out5);
  and and_7 (and_7_out, REG_WRITE_ENABLE, decoder_1_out6);
  and and_8 (and_8_out, REG_WRITE_ENABLE, decoder_1_out7);
  _18_bit_register REG0 (.Input(WRITE_DATA), .Enable(and_1_out), .Clock(Clock), .Clear(Clear), .Output(REG0_output));
  _18_bit_register REG1 (.Input(WRITE_DATA), .Enable(and_2_out), .Clock(Clock), .Clear(Clear), .Output(REG1_output));
  _18_bit_register REG2 (.Input(WRITE_DATA), .Enable(and_3_out), .Clock(Clock), .Clear(Clear), .Output(REG2_output));
  _18_bit_register REG3 (.Input(WRITE_DATA), .Enable(and_4_out), .Clock(Clock), .Clear(Clear), .Output(REG3_output));
  _18_bit_register REG4 (.Input(WRITE_DATA), .Enable(and_5_out), .Clock(Clock), .Clear(Clear), .Output(REG4_output));
  _18_bit_register REG5 (.Input(WRITE_DATA), .Enable(and_6_out), .Clock(Clock), .Clear(Clear), .Output(REG5_output));
  _18_bit_register REG6 (.Input(WRITE_DATA), .Enable(and_7_out), .Clock(Clock), .Clear(Clear), .Output(REG6_output));
  _18_bit_register REG7 (.Input(WRITE_DATA), .Enable(and_8_out), .Clock(Clock), .Clear(Clear), .Output(REG7_output));
  and and_9 (and_9_out, REG_WRITE_ENABLE, decoder_1_out8);
  and and_10 (and_10_out, REG_WRITE_ENABLE, decoder_1_out9);
  and and_11 (and_11_out, REG_WRITE_ENABLE, decoder_1_out10);
  and and_12 (and_12_out, REG_WRITE_ENABLE, decoder_1_out11);
  and and_13 (and_13_out, REG_WRITE_ENABLE, decoder_1_out12);
  and and_14 (and_14_out, REG_WRITE_ENABLE, decoder_1_out13);
  and and_15 (and_15_out, REG_WRITE_ENABLE, decoder_1_out14);
  and and_16 (and_16_out, REG_WRITE_ENABLE, decoder_1_out15);
  _18_bit_register REG8 (.Input(WRITE_DATA), .Enable(and_9_out), .Clock(Clock), .Clear(Clear), .Output(REG8_output));
  _18_bit_register REG9 (.Input(WRITE_DATA), .Enable(and_10_out), .Clock(Clock), .Clear(Clear), .Output(REG9_output));
  _18_bit_register REG10 (.Input(WRITE_DATA), .Enable(and_11_out), .Clock(Clock), .Clear(Clear), .Output(REG10_output));
  _18_bit_register REG11 (.Input(WRITE_DATA), .Enable(and_12_out), .Clock(Clock), .Clear(Clear), .Output(REG11_output));
  _18_bit_register REG12 (.Input(WRITE_DATA), .Enable(and_13_out), .Clock(Clock), .Clear(Clear), .Output(REG12_output));
  _18_bit_register REG13 (.Input(WRITE_DATA), .Enable(and_14_out), .Clock(Clock), .Clear(Clear), .Output(REG13_output));
  _18_bit_register REG14 (.Input(WRITE_DATA), .Enable(and_15_out), .Clock(Clock), .Clear(Clear), .Output(REG14_output));
  _18_bit_register REG15 (.Input(WRITE_DATA), .Enable(and_16_out), .Clock(Clock), .Clear(Clear), .Output(REG15_output));
  Multiplexer #(.select(4), .width(18), .enable("false")) multiplexer_1 (
    .in0(REG0_output), .in1(REG1_output), .in2(REG2_output), .in3(REG3_output), .in4(REG4_output),
    .in5(REG5_output), .in6(REG6_output), .in7(REG7_output), .in8(REG8_output), .in9(REG9_output),
    .in10(REG10_output), .in11(REG11_output), .in12(REG12_output), .in13(REG13_output), .in14(REG14_output),
    .in15(REG15_output), .out(READ_DATA_1), .sel(READ_REG_1));
  Multiplexer #(.select(4), .width(18), .enable("false")) multiplexer_2 (
    .in0(REG0_output), .in1(REG1_output), .in2(REG2_output), .in3(REG3_output), .in4(REG4_output),
    .in5(REG5_output), .in6(REG6_output), .in7(REG7_output), .in8(REG8_output), .in9(REG9_output),
    .in10(REG10_output), .in11(REG11_output), .in12(REG12_output), .in13(REG13_output), .in14(REG14_output),
    .in15(REG15_output), .out(READ_DATA_2), .sel(READ_REG_2));
endmodule

module test (
  input  [17:0] in_1,
  input  in_2,
  input  in_3,
  input  [3:0] in_4,
  input  [3:0] in_5,
  input  in_6,
  input  [3:0] in_7,
  input  in_8,
  input  [3:0] in_9,
  input  in_10,
  input  [17:0] in_11,
  input  in_12,
  output [17:0] out_13,
  output [17:0] out_14,
  output [17:0] out_15
);

  wire register_file_1_p6;
  wire [17:0] n18_bit_register_2_output, n18_bit_register_3_output;

  _18_bit_register u_18_bit_register_1 (.Input(in_1), .Enable(in_3), .Clock(in_2), .Output(out_13));  // open: Clear
  // register_file register_file_1: pin names not known; wires that end beside it: in_4, in_5, in_6, in_8, out_14, register_file_1_p6, register_file_1_p6
  _18_bit_register u_18_bit_register_2 (.Output(n18_bit_register_2_output));  // open: Input, Enable, Clock, Clear
  _18_bit_register u_18_bit_register_3 (.Output(n18_bit_register_3_output));  // open: Input, Enable, Clock, Clear
  // register_file register_file_2: pin names not known; wires that end beside it: in_7, in_9, in_11, in_10, in_12, out_15
endmodule

module control_unit (
  input  [17:0] INPUT
);
endmodule
